# Fritzing sketch more LEDS (saved by Fritzing 0.7.0b)
breadboards: 1

parts:
  LED1 = LED - 5mm [color="Red (633nm)" package="5 mm [THT]"]
  R1 = Resistor [tolerance=±5% resistance=220 package=THT]
  LED2 = LED - 5mm [color="Red (633nm)" package="5 mm [THT]"]
  R2 = Resistor [tolerance=±5% resistance=220 package=THT]
  LED3 = LED - 5mm [color="Red (633nm)" package="5 mm [THT]"]
  R3 = Resistor [tolerance=±5% resistance=220 package=THT]

nets:
  N1: LED1.anode, R1.Pin_0
  N2: R1.Pin_1, R2.Pin_1, R3.Pin_1
  N3: LED2.anode, R2.Pin_0
  N4: LED3.anode, R3.Pin_0

notes:
  To ground on Arduino
  To the Arduino pins
